// Logisim project cpu.circ as structural Verilog: 1 circuit, main circuit cpu
module cpu (
  input  clk,
  input  [31:0] Instruction,
  input  [31:0] MemReadData,
  output [31:0] MemAddress,
  output [31:0] ProgramCounter,
  output [31:0] ra,
  output [31:0] sp,
  output [31:0] t0,
  output [31:0] t1,
  output [31:0] t2,
  output [31:0] s0,
  output [31:0] s1,
  output [31:0] a0,
  output [3:0] MemWriteMask,
  output [31:0] MemWriteData
);

  wire ASel, BrEq, BrLt, BrUn, BSel, PCSel, RegWEn;
  wire [2:0] ImmSel;
  wire [3:0] ALUSel;
  wire [31:0] A_Value, adder_1_out, ALUResult, B_Value, immedimate, PCValue, ReadData1, ReadData2;

  Register #(.width(32)) PC (.D(PCValue), .clk(clk), .Q(ProgramCounter));  // open: en, clr
  Adder #(.width(32)) adder_1 (.a(ProgramCounter), .b(32'h4), .out(adder_1_out));  // open: cin, cout
  Multiplexer #(.width(32)) multiplexer_1 (.in0(adder_1_out), .in1(ALUResult), .out(PCValue), .sel(PCSel));
  control_logic control_logic_1 (
    .Instruction(Instruction), .BrEq(BrEq), .BrLt(BrLt), .PCSel(PCSel), .RegWEn(RegWEn), .ImmSel(ImmSel),
    .BrUn(BrUn), .ASel(ASel), .BSel(BSel), .ALUSel(ALUSel));  // open: MemWEn, WBSel
  regfile regfile_1 (
    .ReadIndex1(Instruction[19:15]), .ReadIndex2(Instruction[24:20]), .WriteIndex(Instruction[11:7]),
    .WriteData(ALUResult), .RegWEn(RegWEn), .clk(clk), .ra(ra), .sp(sp), .t0(t0), .t1(t1), .t2(t2), .s0(s0),
    .s1(s1), .a0(a0), .ReadData1(ReadData1), .ReadData2(ReadData2));
  imm_gen imm_gen_1 (.Instruction(Instruction), .ImmSel(ImmSel), .Immediate(immedimate));
  alu alu_1 (.A(A_Value), .B(B_Value), .ALUSel(ALUSel), .ALUResult(ALUResult));
  branch_comp branch_comp_1 (.BrData1(ReadData1), .BrData2(ReadData2), .BrUn(BrUn), .BrEq(BrEq), .BrLt(BrLt));
  Multiplexer #(.width(32)) multiplexer_2 (.in0(ReadData2), .in1(immedimate), .out(B_Value), .sel(BSel));
  Multiplexer #(.width(32)) multiplexer_3 (.in0(ReadData1), .in1(ProgramCounter), .out(A_Value), .sel(ASel));
  // partial_store partial_store_1: pin names not known
  // partial_load partial_load_1: pin names not known

  // Other names for the same wires on the sheet: opcode[6:0] = Instruction[6:0]; rd[4:0] = Instruction[11:7];
  //   funct3[2:0] = Instruction[14:12]; rs1[4:0] = Instruction[19:15]; rs2[4:0] = Instruction[24:20]

  // Notes on the sheet:
  //   To IMEM
  //   IMEM (do **NOT** move this)
  //   From IMEM
  //   Inputs/Outputs for testing. Do **NOT** move these.
  //   It is OK to move the PC, RegFile, ALU, MEM, Branch Comp, Imm Gen, Partial Load, Partial Store and Control Logic to wherever is most convenient for you when constructing your CPU, and to delete this text
  //   To DMEM
  //   DMEM (do **NOT** move this)
  //   From DMEM
endmodule
